# Fritzing sketch circuit (saved by Fritzing 0.9.9b)
breadboards: 1

parts:
  Mod1 = Raspberry Pi Pico W
  R1 = Rotary Potentiometer (Small) [maximum_resistance=10kΩ package=THT]
  S1 = Pushbutton [package="[THT]"]
  C1 = Electrolytic Capacitor [capacitance=10µF voltage=35V package="1010 [SMD, electrolytic]"]

nets:
  N1: Mod1.pin_3, Mod1.pin_8, Mod1.pin_13, Mod1.pin_18, Mod1.pin_23, Mod1.pin_28, Mod1.pin_33, Mod1.pin_38, R1.leg1, S1.Pin_3, S1.Pin_4, C1.-
  N2: Mod1.pin_30, S1.Pin_1, S1.Pin_2
  N3: Mod1.pin_31, R1.wiper, C1.+
  N4: Mod1.pin_36, R1.leg2

custom parts:
  Raspberry Pi Pico W: Raspberry Pi Pico W. Based around the RP2040 microcontroller the Pico W is a low cost microcontroller device bringing Raspberry Pi quality, cost, and easy of use to the microcontroller space. The areas marked KEEPOUT in pcb silkscreen should not have traces running through them to avoid shorts on a soldered in module!
